# Fritzing sketch Sensor Circuit (saved by Fritzing 0.9.4)
breadboards: 1

parts:
  Part3 = MyoWare Cable Shield
  M1 = Dagu DGServo 9g (Pan and tilt) [part_number=RS001B]
  Part4 = Arduino Pro

nets (from the breadboard view):
  GND: Part3.GND, M1.gnd, Part4.GND
  VCC: Part3.VCC, M1.vcc, Part4.3V3
  N1: Part3.SIG, Part4.A0
  N2: M1.pulse, Part4.D9_PWM

// code stored in the sketch: sketch_oct29a.ino
#include <Servo.h>
Servo servo1;
int ledPin = 13;
int inPin = 7;
int val = 0;
float EMG = A0;

void setup() {
  pinMode(ledPin, OUTPUT);
  pinMode(inPin, INPUT);
  servo1.attach(9, 900, 2100);
  pinMode(EMG, INPUT);
  Serial.begin(9600);
}

void loop() {
  Serial.println(analogRead(A0*5.0/1023.0));
  delay(10);
}
